# Fritzing sketch sketch (saved by Fritzing 0.9.5d)

parts:
  Part1 = Adafruit HUZZAH32 ESP32 Feather [part_number="Adafruit #3405"]
  Part2 = HC-SR501 Body Sensor Module
  U1 = LIPO-110mAh [package=lipo-110]  # not connected
  Capacitive_Soil_Moisture_Sensor1 = DFRobot Capacitive Soil Moisture Sensor V1.0 [part_number=SEN0193]

nets:
  N1: Part1.IO21, Capacitive_Soil_Moisture_Sensor1.A
  N2: Part1.IO17, Capacitive_Soil_Moisture_Sensor1.VCC
  GND: Part1.GND, Part2.GND
  3.3V: Part1.3.3V, Part2.VCC
  N3: Part1.IO15_A8, Part2.OUT

custom parts:
  HC-SR501 Body Sensor Module: Pyroelectric Infrared PIR Motion Sensor Detector Module
  DFRobot Capacitive Soil Moisture Sensor V1.0: DFRobot Capacitive Soil Moisture Sensor V1.0 This product measures soil moisture levels by capacitive sensing, rather than resistive sensing like other types of moisture sensor. It is made of a corrosion resistant material giving it a long service life. Insert it into soil and impress your friends with the real-time soil moisture data! The product includes an on-board voltage regulator which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
